# Fritzing sketch Terrarium_scheme_v1.2 (saved by Fritzing 0.9.3b)
breadboards: 1

parts:
  Часть1 = Arduino Nano (Rev3.0)
  Часть2 = Soil Moisture Sensor
  Часть3 = Soil Moisture Sensor
  Часть4 = Soil Moisture Sensor
  Часть5 = Soil Moisture Sensor
  Grove1 = Grove OLED 128x96

nets:
  GND: Часть1.GND, Часть1.VIN, Часть2.GND, Часть3.GND, Часть4.GND, Часть5.GND, Grove1.GND
  N1: Часть1.D3, Часть2.VCC
  N2: Часть1.D5, Часть3.VCC
  N3: Часть1.D6, Часть4.VCC
  N4: Часть1.D9, Часть5.VCC
  5V: Часть1.5V, Grove1.VCC
  N5: Часть1.A5, Grove1.SCL
  N6: Часть1.A4, Grove1.SDA
  N7: Часть1.A3, Часть5.SIG
  N8: Часть1.A2, Часть4.SIG
  N9: Часть1.A1, Часть3.SIG
  N10: Часть1.A0, Часть2.SIG
